# Fritzing sketch fbape Fritzing (saved by Fritzing 1.0.2b)
breadboards: 2

parts:
  Vidor_4000_MKR = Arduino MKR Vidor 4000
  SD_Card = MicroSD Card Module
  OLED_Display = OLED 128x64 I2C Monochrome Display
  SPDIF_Input = RCA [package=pth]
  Poti_(linear) = Rotary Potentiometer (Small) [maximum_resistance=10kΩ knob_status=50% power=0.5W package=THT]
  IC1 = Microchip MCP23008 8-bit I/O expander [part_number=MCP23008 package="DIP (Dual Inline) [THT]"]
  S1 = JOYSTICK_MINI [package=joystick_mini]
  LED1 = LED - 3mm [color="Green (555nm)" current=30mA package="3 mm [THT]"]
  R2 = Resistor [tolerance=±5% power=0.25W resistance=330 package=THT]
  SPDIF_Output = RCA [package=pth]
  C1 = Ceramic Capacitor [capacitance=540pF voltage=35V package="100 mil [THT, multilayer]"]
  C2 = Ceramic Capacitor [capacitance=540pF voltage=35V package="100 mil [THT, multilayer]"]
  C3 = Ceramic Capacitor [capacitance=540pF voltage=35V package="100 mil [THT, multilayer]"]
  R3 = Resistor [tolerance=±5% power=0.25W resistance=10k package=THT]
  R4 = Resistor [tolerance=±5% power=0.25W resistance=10k package=THT]
  R5 = Resistor [tolerance=±5% power=0.25W resistance=10k package=THT]
  Left/Right = 3.5mm Audio Jack [package=audio-jack-3.5mm-smd]
  Subwoofer = 3.5mm Audio Jack [package=audio-jack-3.5mm-smd]
  WS2812B_Matrix = ws2812b [package="smd 2812b"]
  TI_PCM182x = QFN-20-0.4MM [chip_label=IC package=QFN]
  C4 = Ceramic Capacitor [capacitance=540pF voltage=35V package="100 mil [THT, multilayer]"]
  C5 = Ceramic Capacitor [capacitance=540pF voltage=35V package="100 mil [THT, multilayer]"]
  C6 = Ceramic Capacitor [capacitance=540pF voltage=35V package="100 mil [THT, multilayer]"]

nets:
  N1: Vidor_4000_MKR.AREF, WS2812B_Matrix.DIN
  N2: Vidor_4000_MKR.A0_DAC0, Poti_(linear).wiper
  N3: Vidor_4000_MKR.A3, TI_PCM182x.11
  N4: Vidor_4000_MKR.A4, TI_PCM182x.7
  N5: Vidor_4000_MKR.A5, TI_PCM182x.8
  N6: Vidor_4000_MKR.A6, TI_PCM182x.6
  N7: Vidor_4000_MKR.D2_PWM, R4.Pin_1
  N8: Vidor_4000_MKR.D3_PWM, R3.Pin_1
  N9: Vidor_4000_MKR.D4_PWM, R5.Pin_1
  N10: Vidor_4000_MKR.D5_PWM, SPDIF_Output.PIN
  N11: Vidor_4000_MKR.D6, SPDIF_Input.PIN
  N12: Vidor_4000_MKR.D7, SD_Card.CS
  N13: Vidor_4000_MKR.D8_MOSI, SD_Card.MOSI
  N14: Vidor_4000_MKR.D9_SCK, SD_Card.SCK
  N15: Vidor_4000_MKR.D10_MISO, SD_Card.MISO
  N16: Vidor_4000_MKR.D11_SDA, OLED_Display.SDA, IC1.SDA
  N17: Vidor_4000_MKR.D12_SCL, Vidor_4000_MKR.D13_RX, OLED_Display.SCK, IC1.SCL
  GND: Vidor_4000_MKR.GND, Vidor_4000_MKR.-VBAT, Vidor_4000_MKR.HDMI_2, Vidor_4000_MKR.HDMI_13, Vidor_4000_MKR.HDMI_16, Vidor_4000_MKR.PCI_18, Vidor_4000_MKR.PCI_34, SD_Card.GND, OLED_Display.GND, SPDIF_Input.SHELL, Poti_(linear).leg1, IC1.A2, IC1.A1, IC1.A0, IC1.VSS, S1.GND, SPDIF_Output.SHELL, C1.0, C2.1, C3.0, Left/Right.SLEEVE, Subwoofer.SLEEVE, WS2812B_Matrix.VSS, TI_PCM182x.5, TI_PCM182x.10, TI_PCM182x.12, TI_PCM182x.15, TI_PCM182x.19, TI_PCM182x.20, C4.0, C5.0, C6.0
  VDD: Vidor_4000_MKR.VCC, Vidor_4000_MKR.VIN, Vidor_4000_MKR.PCI_24, SD_Card.VCC, OLED_Display.VDD, Poti_(linear).leg2, IC1.Reset, IC1.VDD, R2.Pin_1, WS2812B_Matrix.VDD, TI_PCM182x.9, TI_PCM182x.13, TI_PCM182x.16
  N18: IC1.GP0, LED1.cathode
  N19: IC1.GP3, S1.CENT
  N20: IC1.GP4, S1.LEFT
  N21: IC1.GP5, S1.DOWN
  N22: IC1.GP6, S1.RIGHT
  N23: IC1.GP7, S1.UP
  N24: LED1.anode, R2.Pin_0
  N25: C1.1, R5.Pin_0, Subwoofer.RIGHT, Subwoofer.LEFT
  N26: C2.0, R3.Pin_0, Left/Right.RIGHT
  N27: C3.1, R4.Pin_0, Left/Right.LEFT
  N28: TI_PCM182x.14, C4.1, C6.1
  N29: TI_PCM182x.17, C5.1

notes:
  UltraNet Ch 1-8
  UltraNet Ch 9-16
  Differential
  Analog Input

custom parts:
  Arduino MKR Vidor 4000: MKR Vidor 4000 contains the Microchip SAMD21 micro controller and a Cyclone 10 FPGA. features: onboard 8 Mbyte SDRAM, 2 Mbyte QSPI Flash (1MB for user applications), Micro HDMI connector, MIPI camera connector, Wifi & BLE powered by U-BLOX NINA W102 module, the classic MKR interface on which all pins are driven both by SAMD21 and FPGA and a MiniPCI Express connector with up to 25 user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
  Microchip MCP23008 8-bit I/O expander: Provides 8-bit, general purpose, parallel I/O expansion for I2C bus. Datasheet: http://ww1.microchip.com/downloads/en/devicedoc/21919e.pdf
